# Fritzing sketch iotnode (saved by Fritzing 0.9.4)
breadboards: 1

parts:
  LED3 = LED - 5mm [color="Green (570nm)" package="5 mm [THT]"]
  LED4 = LED - 5mm [color="Red (635nm)" package="5 mm [THT]"]
  LED5 = LED - 5mm [color="Green (570nm)" package="5 mm [THT]"]
  LED6 = LED - 5mm [color="Green (570nm)" package="5 mm [THT]"]
  LED7 = LED - 5mm [color="Green (570nm)" package="5 mm [THT]"]
  R1 = Resistor [tolerance=±5% resistance=220 package=THT]
  R2 = Resistor [tolerance=±5% resistance=220 package=THT]
  R3 = Resistor [tolerance=±5% resistance=220 package=THT]
  R4 = Resistor [tolerance=±5% resistance=220 package=THT]
  R5 = Resistor [tolerance=±5% resistance=220 package=THT]
  ADC1 = MCP3008 [package=dil16]
  Part1 = KY-019 5V Relay Module [package="Breakout board"]
  MCU1 = Raspberry Pi Zero
  Εξάρτημα1 = Soil Moisture Sensor

nets:
  N1: LED3.cathode, R1.Pin_0
  N2: LED4.cathode, R2.Pin_0
  N3: LED5.cathode, R3.Pin_0
  N4: LED6.cathode, R4.Pin_0
  N5: LED7.cathode, R5.Pin_0
  N6: R1.Pin_1, R2.Pin_1, R4.Pin_1, R5.Pin_1, ADC1.DGND, ADC1.AGND, Part1.-, MCU1.pin_6, MCU1.pin_39, Εξάρτημα1.GND
  N7: ADC1.CH0, Εξάρτημα1.SIG
  VDD: ADC1.VREF, ADC1.VDD, Part1.+, MCU1.pin_1, MCU1.pin_17, Εξάρτημα1.VCC

custom parts:
  KY-019 5V Relay Module: KY-019 5V Relay module, used to control AC circuits.
